// Logisim project Memory.circ as structural Verilog: 5 circuits, main circuit main
module _2x12_MEM (
  input  D0,
  input  D1,
  input  D2,
  input  D3,
  input  D4,
  input  D5,
  input  D6,
  input  D7,
  input  D8,
  input  D9,
  input  D10,
  input  D11,
  input  ADD0,
  input  WE,
  input  ADD1,
  output Q0,
  output Q1,
  output Q2,
  output Q3,
  output Q4,
  output Q5,
  output Q6,
  output Q7,
  output Q8,
  output Q9,
  output Q10,
  output Q11
);

  wire and_1_out, and_2_out, and_3_out, and_4_out, and_5_out, and_6_out, and_7_out, and_8_out, and_9_out,
       and_10_out, and_11_out, and_12_out, and_13_out, and_14_out, and_15_out, and_16_out, and_17_out,
       and_18_out, and_19_out, and_20_out, and_21_out, and_22_out, and_23_out, and_24_out, and_25_out,
       and_26_out, bit_1_q, bit_2_q, bit_3_q, bit_4_q, bit_5_q, bit_6_q, bit_7_q, bit_8_q, bit_9_q, bit_10_q,
       bit_11_q, bit_12_q, bit_13_q, bit_14_q, bit_15_q, bit_16_q, bit_17_q, bit_18_q, bit_19_q, bit_20_q,
       bit_21_q, bit_22_q, bit_23_q, bit_24_q;

  and and_1 (and_1_out, ADD0, WE);
  and and_2 (and_2_out, ADD1, WE);
  BIT bit_1 (.D(D0), .WE(and_1_out), .Q(bit_1_q));
  BIT bit_2 (.D(D0), .WE(and_2_out), .Q(bit_2_q));
  and and_3 (and_3_out, ADD0, bit_1_q);
  and and_4 (and_4_out, ADD1, bit_2_q);
  or or_1 (Q0, and_4_out, and_3_out);
  BIT bit_3 (.D(D1), .WE(and_1_out), .Q(bit_3_q));
  BIT bit_4 (.D(D1), .WE(and_2_out), .Q(bit_4_q));
  and and_5 (and_5_out, ADD0, bit_3_q);
  and and_6 (and_6_out, ADD1, bit_4_q);
  or or_2 (Q1, and_6_out, and_5_out);
  BIT bit_5 (.D(D2), .WE(and_1_out), .Q(bit_5_q));
  BIT bit_6 (.D(D2), .WE(and_2_out), .Q(bit_6_q));
  and and_7 (and_7_out, ADD0, bit_5_q);
  and and_8 (and_8_out, ADD1, bit_6_q);
  or or_3 (Q2, and_8_out, and_7_out);
  BIT bit_7 (.D(D3), .WE(and_1_out), .Q(bit_7_q));
  BIT bit_8 (.D(D3), .WE(and_2_out), .Q(bit_8_q));
  and and_9 (and_9_out, ADD0, bit_7_q);
  and and_10 (and_10_out, ADD1, bit_8_q);
  or or_4 (Q3, and_10_out, and_9_out);
  BIT bit_9 (.D(D4), .WE(and_1_out), .Q(bit_9_q));
  BIT bit_10 (.D(D4), .WE(and_2_out), .Q(bit_10_q));
  and and_11 (and_11_out, ADD0, bit_9_q);
  and and_12 (and_12_out, ADD1, bit_10_q);
  or or_5 (Q4, and_12_out, and_11_out);
  BIT bit_11 (.D(D5), .WE(and_1_out), .Q(bit_11_q));
  BIT bit_12 (.D(D5), .WE(and_2_out), .Q(bit_12_q));
  and and_13 (and_13_out, ADD0, bit_11_q);
  and and_14 (and_14_out, ADD1, bit_12_q);
  or or_6 (Q5, and_14_out, and_13_out);
  BIT bit_13 (.D(D6), .WE(and_1_out), .Q(bit_13_q));
  BIT bit_14 (.D(D6), .WE(and_2_out), .Q(bit_14_q));
  and and_15 (and_15_out, ADD0, bit_13_q);
  and and_16 (and_16_out, ADD1, bit_14_q);
  or or_7 (Q6, and_16_out, and_15_out);
  BIT bit_15 (.D(D7), .WE(and_1_out), .Q(bit_15_q));
  BIT bit_16 (.D(D7), .WE(and_2_out), .Q(bit_16_q));
  and and_17 (and_17_out, ADD0, bit_15_q);
  and and_18 (and_18_out, ADD1, bit_16_q);
  or or_8 (Q7, and_18_out, and_17_out);
  BIT bit_17 (.D(D8), .WE(and_1_out), .Q(bit_17_q));
  BIT bit_18 (.D(D8), .WE(and_2_out), .Q(bit_18_q));
  and and_19 (and_19_out, ADD0, bit_17_q);
  and and_20 (and_20_out, ADD1, bit_18_q);
  or or_9 (Q8, and_20_out, and_19_out);
  BIT bit_19 (.D(D9), .WE(and_1_out), .Q(bit_19_q));
  BIT bit_20 (.D(D9), .WE(and_2_out), .Q(bit_20_q));
  and and_21 (and_21_out, ADD0, bit_19_q);
  and and_22 (and_22_out, ADD1, bit_20_q);
  BIT bit_21 (.D(D10), .WE(and_1_out), .Q(bit_21_q));
  BIT bit_22 (.D(D10), .WE(and_2_out), .Q(bit_22_q));
  or or_10 (Q9, and_22_out, and_21_out);
  and and_23 (and_23_out, ADD0, bit_21_q);
  and and_24 (and_24_out, ADD1, bit_22_q);
  or or_11 (Q10, and_24_out, and_23_out);
  BIT bit_23 (.D(D11), .WE(and_1_out), .Q(bit_23_q));
  BIT bit_24 (.D(D11), .WE(and_2_out), .Q(bit_24_q));
  and and_25 (and_25_out, ADD0, bit_23_q);
  and and_26 (and_26_out, ADD1, bit_24_q);
  or or_12 (Q11, and_26_out, and_25_out);
endmodule

module BIT (
  input  D,
  input  WE,
  output Q
);

  wire nand_1_out, nand_2_out, nand_4_out, not_1_out;

  not not_1 (not_1_out, D);
  nand nand_1 (nand_1_out, D, WE);
  nand nand_2 (nand_2_out, WE, not_1_out);
  nand nand_3 (Q, nand_1_out, nand_4_out);
  nand nand_4 (nand_4_out, Q, nand_2_out);
endmodule

module MEM_UNIT (
  input  D0,
  input  D11,
  input  D1,
  input  D10,
  input  D2,
  input  D9,
  input  D3,
  input  D8,
  input  D4,
  input  D7,
  input  D5,
  input  D6,
  input  WE,
  input  ADD0,
  input  ADD1,
  input  ADD2,
  input  ADD3,
  output Q0,
  output Q1,
  output Q2,
  output Q3,
  output Q4,
  output Q5,
  output Q6,
  output Q7,
  output Q8,
  output Q9,
  output Q10,
  output Q11
);

  wire n2x12_mem_1_q0, n2x12_mem_1_q1, n2x12_mem_1_q2, n2x12_mem_1_q3, n2x12_mem_1_q4, n2x12_mem_1_q5,
       n2x12_mem_1_q6, n2x12_mem_1_q7, n2x12_mem_1_q8, n2x12_mem_1_q9, n2x12_mem_1_q10, n2x12_mem_1_q11,
       n2x12_mem_2_q0, n2x12_mem_2_q1, n2x12_mem_2_q2, n2x12_mem_2_q3, n2x12_mem_2_q4, n2x12_mem_2_q5,
       n2x12_mem_2_q6, n2x12_mem_2_q7, n2x12_mem_2_q8, n2x12_mem_2_q9, n2x12_mem_2_q10, n2x12_mem_2_q11,
       n2x12_mem_3_q0, n2x12_mem_3_q1, n2x12_mem_3_q2, n2x12_mem_3_q3, n2x12_mem_3_q4, n2x12_mem_3_q5,
       n2x12_mem_3_q6, n2x12_mem_3_q7, n2x12_mem_3_q8, n2x12_mem_3_q9, n2x12_mem_3_q10, n2x12_mem_3_q11,
       n2x12_mem_4_q0, n2x12_mem_4_q1, n2x12_mem_4_q2, n2x12_mem_4_q3, n2x12_mem_4_q4, n2x12_mem_4_q5,
       n2x12_mem_4_q6, n2x12_mem_4_q7, n2x12_mem_4_q8, n2x12_mem_4_q9, n2x12_mem_4_q10, n2x12_mem_4_q11,
       n2x12_mem_5_q0, n2x12_mem_5_q1, n2x12_mem_5_q2, n2x12_mem_5_q3, n2x12_mem_5_q4, n2x12_mem_5_q5,
       n2x12_mem_5_q6, n2x12_mem_5_q7, n2x12_mem_5_q8, n2x12_mem_5_q9, n2x12_mem_5_q10, n2x12_mem_5_q11,
       n2x12_mem_6_q0, n2x12_mem_6_q1, n2x12_mem_6_q2, n2x12_mem_6_q3, n2x12_mem_6_q4, n2x12_mem_6_q5,
       n2x12_mem_6_q6, n2x12_mem_6_q7, n2x12_mem_6_q8, n2x12_mem_6_q9, n2x12_mem_6_q10, n2x12_mem_6_q11,
       n2x12_mem_7_q0, n2x12_mem_7_q1, n2x12_mem_7_q2, n2x12_mem_7_q3, n2x12_mem_7_q4, n2x12_mem_7_q5,
       n2x12_mem_7_q6, n2x12_mem_7_q7, n2x12_mem_7_q8, n2x12_mem_7_q9, n2x12_mem_7_q10, n2x12_mem_7_q11,
       n2x12_mem_8_q0, n2x12_mem_8_q1, n2x12_mem_8_q2, n2x12_mem_8_q3, n2x12_mem_8_q4, n2x12_mem_8_q5,
       n2x12_mem_8_q6, n2x12_mem_8_q7, n2x12_mem_8_q8, n2x12_mem_8_q9, n2x12_mem_8_q10, n2x12_mem_8_q11,
       n4x16_dec_1__14, n4x16_dec_1_y0, n4x16_dec_1_y1, n4x16_dec_1_y2, n4x16_dec_1_y3, n4x16_dec_1_y4,
       n4x16_dec_1_y5, n4x16_dec_1_y6, n4x16_dec_1_y7, n4x16_dec_1_y8, n4x16_dec_1_y9, n4x16_dec_1_y10,
       n4x16_dec_1_y11, n4x16_dec_1_y12, n4x16_dec_1_y13, n4x16_dec_1_y15;

  _4x16_DEC u_4x16_dec_1 (
    .Y0(n4x16_dec_1_y0), .Y1(n4x16_dec_1_y1), .Y2(n4x16_dec_1_y2), .Y3(n4x16_dec_1_y3), .Y4(n4x16_dec_1_y4),
    .Y5(n4x16_dec_1_y5), .Y6(n4x16_dec_1_y6), .Y7(n4x16_dec_1_y7), .Y8(n4x16_dec_1_y8), .Y9(n4x16_dec_1_y9),
    .Y10(n4x16_dec_1_y10), .Y11(n4x16_dec_1_y11), .Y12(n4x16_dec_1_y12), .Y13(n4x16_dec_1_y13),
    ._14(n4x16_dec_1__14), .Y15(n4x16_dec_1_y15), .A0(ADD0), .A1(ADD1), .A2(ADD2), .A3(ADD3));
  _2x12_MEM u_2x12_mem_1 (
    .WE(WE), .ADD0(n4x16_dec_1_y0), .D0(D0), .D1(D0), .D2(D0), .D3(D0), .D4(D0), .D5(D0), .D6(D0), .D7(D0),
    .D8(D0), .D9(D0), .D10(D10), .D11(D11), .Q0(n2x12_mem_1_q0), .Q1(n2x12_mem_1_q1), .Q2(n2x12_mem_1_q2),
    .Q3(n2x12_mem_1_q3), .Q4(n2x12_mem_1_q4), .Q5(n2x12_mem_1_q5), .Q6(n2x12_mem_1_q6), .Q7(n2x12_mem_1_q7),
    .Q8(n2x12_mem_1_q8), .Q9(n2x12_mem_1_q9), .Q10(n2x12_mem_1_q10), .Q11(n2x12_mem_1_q11),
    .ADD1(n4x16_dec_1_y1));
  or or_1 (Q0, n2x12_mem_1_q0, n2x12_mem_2_q0, n2x12_mem_3_q0, n2x12_mem_4_q0, n2x12_mem_5_q0, n2x12_mem_6_q0, n2x12_mem_7_q0, n2x12_mem_8_q0);
  _2x12_MEM u_2x12_mem_2 (
    .WE(WE), .ADD0(n4x16_dec_1_y2), .D0(D0), .D1(D0), .D2(D0), .D3(D0), .D4(D0), .D5(D0), .D6(D0), .D7(D0),
    .D8(D0), .D9(D0), .D10(D10), .D11(D11), .Q0(n2x12_mem_2_q0), .Q1(n2x12_mem_2_q1), .Q2(n2x12_mem_2_q2),
    .Q3(n2x12_mem_2_q3), .Q4(n2x12_mem_2_q4), .Q5(n2x12_mem_2_q5), .Q6(n2x12_mem_2_q6), .Q7(n2x12_mem_2_q7),
    .Q8(n2x12_mem_2_q8), .Q9(n2x12_mem_2_q9), .Q10(n2x12_mem_2_q10), .Q11(n2x12_mem_2_q11),
    .ADD1(n4x16_dec_1_y3));
  or or_2 (Q1, n2x12_mem_1_q1, n2x12_mem_2_q1, n2x12_mem_3_q1, n2x12_mem_4_q1, n2x12_mem_5_q1, n2x12_mem_6_q1, n2x12_mem_7_q1, n2x12_mem_8_q1);
  _2x12_MEM u_2x12_mem_3 (
    .WE(WE), .ADD0(n4x16_dec_1_y4), .D0(D0), .D1(D0), .D2(D0), .D3(D0), .D4(D0), .D5(D0), .D6(D0), .D7(D0),
    .D8(D0), .D9(D0), .D10(D10), .D11(D11), .Q0(n2x12_mem_3_q0), .Q1(n2x12_mem_3_q1), .Q2(n2x12_mem_3_q2),
    .Q3(n2x12_mem_3_q3), .Q4(n2x12_mem_3_q4), .Q5(n2x12_mem_3_q5), .Q6(n2x12_mem_3_q6), .Q7(n2x12_mem_3_q7),
    .Q8(n2x12_mem_3_q8), .Q9(n2x12_mem_3_q9), .Q10(n2x12_mem_3_q10), .Q11(n2x12_mem_3_q11),
    .ADD1(n4x16_dec_1_y5));
  or or_3 (Q2, n2x12_mem_1_q2, n2x12_mem_2_q2, n2x12_mem_3_q2, n2x12_mem_4_q2, n2x12_mem_5_q2, n2x12_mem_6_q2, n2x12_mem_7_q2, n2x12_mem_8_q2);
  or or_4 (Q3, n2x12_mem_1_q3, n2x12_mem_2_q3, n2x12_mem_3_q3, n2x12_mem_4_q3, n2x12_mem_5_q3, n2x12_mem_6_q3, n2x12_mem_7_q3, n2x12_mem_8_q3);
  _2x12_MEM u_2x12_mem_4 (
    .WE(WE), .ADD0(n4x16_dec_1_y6), .D0(D0), .D1(D0), .D2(D0), .D3(D0), .D4(D0), .D5(D0), .D6(D0), .D7(D0),
    .D8(D0), .D9(D0), .D10(D10), .D11(D11), .Q0(n2x12_mem_4_q0), .Q1(n2x12_mem_4_q1), .Q2(n2x12_mem_4_q2),
    .Q3(n2x12_mem_4_q3), .Q4(n2x12_mem_4_q4), .Q5(n2x12_mem_4_q5), .Q6(n2x12_mem_4_q6), .Q7(n2x12_mem_4_q7),
    .Q8(n2x12_mem_4_q8), .Q9(n2x12_mem_4_q9), .Q10(n2x12_mem_4_q10), .Q11(n2x12_mem_4_q11),
    .ADD1(n4x16_dec_1_y7));
  or or_5 (Q4, n2x12_mem_1_q4, n2x12_mem_2_q4, n2x12_mem_3_q4, n2x12_mem_4_q4, n2x12_mem_5_q4, n2x12_mem_6_q4, n2x12_mem_7_q4, n2x12_mem_8_q4);
  _2x12_MEM u_2x12_mem_5 (
    .WE(WE), .ADD0(n4x16_dec_1_y8), .D0(D0), .D1(D0), .D2(D0), .D3(D0), .D4(D0), .D5(D0), .D6(D0), .D7(D0),
    .D8(D0), .D9(D0), .D10(D10), .D11(D11), .Q0(n2x12_mem_5_q0), .Q1(n2x12_mem_5_q1), .Q2(n2x12_mem_5_q2),
    .Q3(n2x12_mem_5_q3), .Q4(n2x12_mem_5_q4), .Q5(n2x12_mem_5_q5), .Q6(n2x12_mem_5_q6), .Q7(n2x12_mem_5_q7),
    .Q8(n2x12_mem_5_q8), .Q9(n2x12_mem_5_q9), .Q10(n2x12_mem_5_q10), .Q11(n2x12_mem_5_q11),
    .ADD1(n4x16_dec_1_y9));
  or or_6 (Q5, n2x12_mem_1_q5, n2x12_mem_2_q5, n2x12_mem_3_q5, n2x12_mem_4_q5, n2x12_mem_5_q5, n2x12_mem_6_q5, n2x12_mem_7_q5, n2x12_mem_8_q5);
  or or_7 (Q6, n2x12_mem_1_q6, n2x12_mem_2_q6, n2x12_mem_3_q6, n2x12_mem_4_q6, n2x12_mem_5_q6, n2x12_mem_6_q6, n2x12_mem_7_q6, n2x12_mem_8_q6);
  _2x12_MEM u_2x12_mem_6 (
    .WE(WE), .ADD0(n4x16_dec_1_y10), .D0(D0), .D1(D0), .D2(D0), .D3(D0), .D4(D0), .D5(D0), .D6(D0), .D7(D0),
    .D8(D0), .D9(D0), .D10(D10), .D11(D11), .Q0(n2x12_mem_6_q0), .Q1(n2x12_mem_6_q1), .Q2(n2x12_mem_6_q2),
    .Q3(n2x12_mem_6_q3), .Q4(n2x12_mem_6_q4), .Q5(n2x12_mem_6_q5), .Q6(n2x12_mem_6_q6), .Q7(n2x12_mem_6_q7),
    .Q8(n2x12_mem_6_q8), .Q9(n2x12_mem_6_q9), .Q10(n2x12_mem_6_q10), .Q11(n2x12_mem_6_q11),
    .ADD1(n4x16_dec_1_y11));
  or or_8 (Q7, n2x12_mem_1_q7, n2x12_mem_2_q7, n2x12_mem_3_q7, n2x12_mem_4_q7, n2x12_mem_5_q7, n2x12_mem_6_q7, n2x12_mem_7_q7, n2x12_mem_8_q7);
  _2x12_MEM u_2x12_mem_7 (
    .WE(WE), .ADD0(n4x16_dec_1_y12), .D0(D0), .D1(D0), .D2(D0), .D3(D0), .D4(D0), .D5(D0), .D6(D0), .D7(D0),
    .D8(D0), .D9(D0), .D10(D10), .D11(D11), .Q0(n2x12_mem_7_q0), .Q1(n2x12_mem_7_q1), .Q2(n2x12_mem_7_q2),
    .Q3(n2x12_mem_7_q3), .Q4(n2x12_mem_7_q4), .Q5(n2x12_mem_7_q5), .Q6(n2x12_mem_7_q6), .Q7(n2x12_mem_7_q7),
    .Q8(n2x12_mem_7_q8), .Q9(n2x12_mem_7_q9), .Q10(n2x12_mem_7_q10), .Q11(n2x12_mem_7_q11),
    .ADD1(n4x16_dec_1_y13));
  or or_9 (Q8, n2x12_mem_1_q8, n2x12_mem_2_q8, n2x12_mem_3_q8, n2x12_mem_4_q8, n2x12_mem_5_q8, n2x12_mem_6_q8, n2x12_mem_7_q8, n2x12_mem_8_q8);
  _2x12_MEM u_2x12_mem_8 (
    .WE(WE), .ADD0(n4x16_dec_1__14), .D0(D0), .D1(D0), .D2(D0), .D3(D0), .D4(D0), .D5(D0), .D6(D0), .D7(D0),
    .D8(D0), .D9(D0), .D10(D10), .D11(D11), .Q0(n2x12_mem_8_q0), .Q1(n2x12_mem_8_q1), .Q2(n2x12_mem_8_q2),
    .Q3(n2x12_mem_8_q3), .Q4(n2x12_mem_8_q4), .Q5(n2x12_mem_8_q5), .Q6(n2x12_mem_8_q6), .Q7(n2x12_mem_8_q7),
    .Q8(n2x12_mem_8_q8), .Q9(n2x12_mem_8_q9), .Q10(n2x12_mem_8_q10), .Q11(n2x12_mem_8_q11),
    .ADD1(n4x16_dec_1_y15));
  or or_10 (Q9, n2x12_mem_1_q9, n2x12_mem_2_q9, n2x12_mem_3_q9, n2x12_mem_4_q9, n2x12_mem_5_q9, n2x12_mem_6_q9, n2x12_mem_7_q9, n2x12_mem_8_q9);
  or or_11 (Q10, n2x12_mem_1_q10, n2x12_mem_2_q10, n2x12_mem_3_q10, n2x12_mem_4_q10, n2x12_mem_5_q10, n2x12_mem_6_q10, n2x12_mem_7_q10, n2x12_mem_8_q10);
  or or_12 (Q11, n2x12_mem_1_q11, n2x12_mem_2_q11, n2x12_mem_3_q11, n2x12_mem_4_q11, n2x12_mem_5_q11, n2x12_mem_6_q11, n2x12_mem_7_q11, n2x12_mem_8_q11);

  assign D1 = D0;
  assign D2 = D0;
  assign D3 = D0;
  assign D4 = D0;
  assign D5 = D0;
  assign D6 = D0;
  assign D7 = D0;
  assign D8 = D0;
  assign D9 = D0;
endmodule

module _4x16_DEC (
  input  A0,
  input  A1,
  input  A2,
  input  A3,
  output Y0,
  output Y1,
  output Y2,
  output Y3,
  output Y4,
  output Y5,
  output Y6,
  output Y7,
  output Y8,
  output Y9,
  output Y10,
  output Y11,
  output Y12,
  output Y13,
  output _14,
  output Y15
);

  wire not_1_out, not_2_out, not_3_out, not_4_out;

  not not_1 (not_1_out, A0);
  not not_2 (not_2_out, A1);
  not not_3 (not_3_out, A2);
  not not_4 (not_4_out, A3);
  and and_1 (Y0, not_4_out, not_3_out, not_2_out, not_1_out);
  and and_2 (Y1, A3, not_3_out, not_2_out, not_1_out);
  and and_3 (Y2, not_4_out, A2, not_2_out, not_1_out);
  and and_4 (Y3, A3, A2, not_2_out, not_1_out);
  and and_5 (Y4, not_4_out, not_3_out, A1, not_1_out);
  and and_6 (Y5, A3, not_3_out, A1, not_1_out);
  and and_7 (Y6, not_4_out, A2, A1, not_1_out);
  and and_8 (Y7, A3, A2, A1, not_1_out);
  and and_9 (Y8, not_4_out, not_3_out, not_2_out, A0);
  and and_10 (Y9, A3, not_3_out, not_2_out, A0);
  and and_11 (Y10, not_4_out, A2, not_2_out, A0);
  and and_12 (Y11, A3, A2, not_2_out, A0);
  and and_13 (Y12, not_4_out, not_3_out, A1, A0);
  and and_14 (Y13, A3, not_3_out, A1, A0);
  and and_15 (_14, not_4_out, A2, A1, A0);
  and and_16 (Y15, A3, A2, A1, A0);
endmodule

module main (
);

  MEM_UNIT mem_unit_1 ();  // open: WE, ADD0, ADD1, ADD2, ADD3, Q4, Q5, Q6, Q7, Q8, Q9, Q10, Q11, D0, D1, D2, D3, D4, D5, D6, D7, D8, D9, D10, D11, Q0, Q1, Q2, Q3
endmodule
